// Logisim project FAeFS.circ as structural Verilog: 5 circuits, main circuit HA
module HA (
  input  B,
  input  A,
  input  in_3,
  output Cout,
  output S
);

  and and_1 (Cout, B, A);
  xor xor_1 (S, B, A);

  // Notes on the sheet:
  //   MEIO SOMADOR
endmodule

module FA3b (
  input  A1,
  input  A0,
  input  C0,
  input  B0,
  input  B1,
  input  A1_2,
  input  A2,
  input  A0_2,
  input  C0_2,
  input  B0_2,
  input  B1_2,
  input  B2,
  output S0,
  output S1,
  output C2,
  output S0_2,
  output S1_2,
  output S2,
  output C4
);

  wire and_1_out, and_2_out, and_3_out, and_4_out, and_5_out, and_6_out, and_7_out, and_8_out, and_9_out,
       and_10_out, and_11_out, and_12_out, and_13_out, and_14_out, and_15_out, or_1_out, or_2_out, or_3_out,
       xor_1_out, xor_2_out, xor_5_out, xor_7_out, xor_10_out;

  xor xor_1 (xor_1_out, B0_2, C0_2);
  and and_1 (and_1_out, C0_2, B0_2);
  and and_2 (and_2_out, B0_2, A0_2);
  and and_3 (and_3_out, C0_2, A0_2);
  xor xor_2 (xor_2_out, B0, C0);
  and and_4 (and_4_out, C0, B0);
  and and_5 (and_5_out, B0, A0);
  and and_6 (and_6_out, C0, A0);
  xor xor_3 (S0_2, A0_2, xor_1_out);
  or or_1 (or_1_out, and_1_out, and_2_out, and_3_out);
  xor xor_4 (S0, A0, xor_2_out);
  or or_2 (or_2_out, and_4_out, and_5_out, and_6_out);
  and and_7 (and_7_out, or_1_out, B1_2);
  and and_8 (and_8_out, B1_2, A1_2);
  and and_9 (and_9_out, or_1_out, A1_2);
  xor xor_5 (xor_5_out, B1, or_2_out);
  and and_10 (and_10_out, or_2_out, B1);
  and and_11 (and_11_out, B1, A1);
  and and_12 (and_12_out, or_2_out, A1);
  xor xor_6 (S1_2, A1_2, xor_7_out);
  xor xor_7 (xor_7_out, B1_2, or_1_out);
  or or_3 (or_3_out, and_7_out, and_8_out, and_9_out);
  xor xor_8 (S1, A1, xor_5_out);
  or or_4 (C2, and_10_out, and_11_out, and_12_out);
  and and_13 (and_13_out, or_3_out, B2);
  and and_14 (and_14_out, B2, A2);
  and and_15 (and_15_out, or_3_out, A2);
  xor xor_9 (S2, A2, xor_10_out);
  xor xor_10 (xor_10_out, B2, or_3_out);
  or or_5 (C4, and_13_out, and_14_out, and_15_out);

  // Notes on the sheet:
  //   SOMADOR DE 3 BITS
  //   SOMADOR DE 2 BITS
  //   BITS DO PRIMEIRO NUMERO
  //   C1
  //   BITS DO PRIMEIRO NUMERO
  //   C1
  //   BITS DO SEGUNDO NUMERO
  //   BITS DO SEGUNDO NUMERO
  //   C2
  //   C3
endmodule

module FS3b (
  input  A1,
  input  A2,
  input  A0,
  input  C0,
  input  in_5,
  input  in_6,
  input  in_7,
  output S0,
  output S1,
  output S2,
  output C4
);

  wire and_1_out, and_2_out, and_3_out, and_4_out, and_5_out, and_6_out, and_7_out, and_8_out, and_9_out,
       not_1_out, not_2_out, not_3_out, or_1_out, or_2_out, xor_1_out, xor_3_out, xor_5_out;

  not not_1 (not_1_out, in_5);
  xor xor_1 (xor_1_out, not_1_out, C0);
  and and_1 (and_1_out, C0, not_1_out);
  and and_2 (and_2_out, not_1_out, A0);
  and and_3 (and_3_out, C0, A0);
  xor xor_2 (S0, A0, xor_1_out);
  or or_1 (or_1_out, and_1_out, and_2_out, and_3_out);
  not not_2 (not_2_out, in_6);
  xor xor_3 (xor_3_out, not_2_out, or_1_out);
  and and_4 (and_4_out, or_1_out, not_2_out);
  and and_5 (and_5_out, not_2_out, A1);
  and and_6 (and_6_out, or_1_out, A1);
  xor xor_4 (S1, A1, xor_3_out);
  or or_2 (or_2_out, and_4_out, and_5_out, and_6_out);
  not not_3 (not_3_out, in_7);
  xor xor_5 (xor_5_out, not_3_out, or_2_out);
  and and_7 (and_7_out, or_2_out, not_3_out);
  and and_8 (and_8_out, not_3_out, A2);
  and and_9 (and_9_out, or_2_out, A2);
  xor xor_6 (S2, A2, xor_5_out);
  or or_3 (C4, and_7_out, and_8_out, and_9_out);

  // Notes on the sheet:
  //   B0
  //   BITS DO MINUENDO
  //   C1
  //   SUBTRATOR EM COMPLEMENTO DE 2
  //   B1
  //   BITS DO SUBTRAENDO
  //   C2
  //   C3
  //   B2
endmodule

module FA (
  input  A0,
  input  C0,
  input  B0,
  output S0,
  output Cout
);

  wire and_1_out, and_2_out, and_3_out, xor_1_out;

  xor xor_1 (xor_1_out, B0, C0);
  and and_1 (and_1_out, C0, B0);
  and and_2 (and_2_out, B0, A0);
  and and_3 (and_3_out, C0, A0);
  xor xor_2 (S0, A0, xor_1_out);
  or or_1 (Cout, and_1_out, and_2_out, and_3_out);
endmodule

module teste (
  input  in_1,
  input  in_2,
  input  in_3,
  input  in_4,
  input  in_5,
  input  in_6,
  input  in_7,
  output out_8,
  output out_9,
  output out_10,
  output out_11
);

  wire fa_1_cout, fa_2_cout;

  FA fa_1 (.A0(in_1), .C0(in_4), .B0(in_5), .S0(out_8), .Cout(fa_1_cout));
  FA fa_2 (.A0(in_2), .C0(fa_1_cout), .B0(in_6), .S0(out_9), .Cout(fa_2_cout));
  FA fa_3 (.A0(in_3), .C0(fa_2_cout), .B0(in_7), .S0(out_10), .Cout(out_11));
endmodule
