// Logisim project LTeULA.circ as structural Verilog: 7 circuits, main circuit main
module main (
  input  in_1,
  input  in_2,
  input  in_3,
  input  in_4,
  input  in_5,
  input  in_6,
  input  in_7,
  input  in_8,
  input  in_9
);

  wire subtrator_1_cout, subtrator_2_cout, subtrator_3_cout, subtrator_4_cout;

  SUBTRATOR subtrator_1 (.A(in_1), .Cin(in_5), .B(in_6), .Cout(subtrator_1_cout));  // open: S
  SUBTRATOR subtrator_2 (.A(in_2), .Cin(subtrator_1_cout), .B(in_7), .Cout(subtrator_2_cout));  // open: S
  SUBTRATOR subtrator_3 (.A(in_3), .Cin(subtrator_2_cout), .B(in_8), .Cout(subtrator_3_cout));  // open: S
  SUBTRATOR subtrator_4 (.A(in_4), .Cin(subtrator_3_cout), .B(in_9), .Cout(subtrator_4_cout));  // open: S
endmodule

module COMPARADOR_LT (
  input  A3,
  input  A2,
  input  A1,
  input  A0,
  input  Cin0,
  input  B3,
  input  B2,
  input  B1,
  input  B0,
  output S0,
  output S1,
  output S2,
  output S3,
  output Cout
);

  wire and_1_out, and_2_out, and_3_out, and_4_out, and_5_out, and_6_out, and_7_out, and_8_out, and_9_out,
       and_10_out, and_11_out, and_12_out, not_1_out, not_2_out, not_3_out, not_4_out, not_5_out, not_6_out,
       not_7_out, not_8_out, or_1_out, or_2_out, or_3_out, xor_1_out, xor_3_out, xor_5_out, xor_7_out;

  not not_1 (not_1_out, A0);
  not not_2 (not_2_out, A0);
  xor xor_1 (xor_1_out, A0, B0);
  and and_1 (and_1_out, not_1_out, B0);
  and and_2 (and_2_out, not_2_out, Cin0, Cin0);
  and and_3 (and_3_out, B0, Cin0);
  xor xor_2 (S0, Cin0, xor_1_out);
  or or_1 (or_1_out, and_1_out, and_2_out, and_3_out);
  not not_3 (not_3_out, A1);
  not not_4 (not_4_out, A1);
  xor xor_3 (xor_3_out, A1, B1);
  and and_4 (and_4_out, not_3_out, B1);
  and and_5 (and_5_out, not_4_out, or_1_out, or_1_out);
  and and_6 (and_6_out, B1, or_1_out);
  xor xor_4 (S1, or_1_out, xor_3_out);
  or or_2 (or_2_out, and_4_out, and_5_out, and_6_out);
  not not_5 (not_5_out, A2);
  not not_6 (not_6_out, A2);
  xor xor_5 (xor_5_out, A2, B2);
  and and_7 (and_7_out, not_5_out, B2);
  and and_8 (and_8_out, not_6_out, or_2_out, or_2_out);
  and and_9 (and_9_out, B2, or_2_out);
  xor xor_6 (S2, or_2_out, xor_5_out);
  or or_3 (or_3_out, and_7_out, and_8_out, and_9_out);
  not not_7 (not_7_out, A3);
  not not_8 (not_8_out, A3);
  xor xor_7 (xor_7_out, A3, B3);
  and and_10 (and_10_out, not_7_out, B3);
  and and_11 (and_11_out, not_8_out, or_3_out, or_3_out);
  and and_12 (and_12_out, B3, or_3_out);
  xor xor_8 (S3, or_3_out, xor_7_out);
  or or_4 (Cout, and_10_out, and_11_out, and_12_out);

  // Notes on the sheet:
  //   Cin1
  //   Cin2
  //   Cin3
endmodule

module ULA (
  input  A,
  input  B,
  input  ALUctrl0,
  input  ALUctrl,
  output Cout
);

  wire adder_1_out, and_1_out, multiplexer_1_out, multiplexer_2_out, not_1_out, or_1_out;

  or or_1 (or_1_out, A, B);
  and and_1 (and_1_out, A, B);
  Multiplexer #(.select(2)) multiplexer_1 (
    .in0(or_1_out), .in1(and_1_out), .in2(adder_1_out), .in3(adder_1_out), .out(multiplexer_1_out),
    .en(ALUctrl));  // open: sel
  not not_1 (not_1_out, B);
  Multiplexer multiplexer_2 (.in0(not_1_out), .in1(B), .out(multiplexer_2_out), .en(ALUctrl0));  // open: sel
  Adder #(.width(1)) adder_1 (.a(multiplexer_2_out), .b(A), .out(adder_1_out), .cin(ALUctrl0), .cout(Cout));
endmodule

module ULA2 (
  input  A,
  input  B,
  input  SUM31,
  input  ALUctrl1
);

  wire adder_1_cout, and_1_out, and_2_out, and_3_out, multiplexer_1_out, multiplexer_2_out, not_1_out,
       not_2_out, not_3_out, or_1_out, undriven, xnor_1_out, xor_1_out;
  wire [7:0] undriven_2;

  NotExactlyOne xnor_1 (.out(xnor_1_out), .in1(undriven), .in2(A), .in3(B));
  xor xor_1 (xor_1_out, A, SUM31);
  and and_1 (and_1_out, xnor_1_out, xor_1_out, not_1_out);
  not not_1 (not_1_out, ALUctrl1);
  and and_2 (and_2_out, not_1_out, undriven_2[0]);
  or or_1 (or_1_out, A, B);
  and and_3 (and_3_out, A, B);
  not not_2 (not_2_out, multiplexer_1_out);
  // AND_Gate and_4 has open pins: in2=not_2_out, out=open
  not not_3 (not_3_out, B);
  Multiplexer #(.select(2)) multiplexer_1 (
    .in0(or_1_out), .in1(and_3_out), .in2(adder_1_cout), .in3(adder_1_cout), .out(multiplexer_1_out));  // open: sel, en
  Multiplexer multiplexer_2 (.in0(not_3_out), .in1(B), .out(multiplexer_2_out));  // open: sel, en
  Adder adder_1 (.b(undriven_2), .cin(multiplexer_2_out), .cout(adder_1_cout));  // open: a, out
  // Pins of 1 and 8 bits meet at undriven_2
endmodule

module somador (
  input  A0,
  input  Cin0,
  input  B0,
  output out_4,
  output Cin1
);

  wire and_1_out, and_2_out, and_3_out, xor_1_out;

  xor xor_1 (xor_1_out, Cin0, B0);
  and and_1 (and_1_out, A0, B0);
  and and_2 (and_2_out, A0, Cin0, Cin0);
  and and_3 (and_3_out, B0, Cin0);
  xor xor_2 (out_4, A0, xor_1_out);
  or or_1 (Cin1, and_1_out, and_2_out, and_3_out);
endmodule

module SUBTRATOR (
  input  A,
  input  Cin,
  input  B,
  output S,
  output Cout
);

  wire and_1_out, and_2_out, and_3_out, not_1_out, not_2_out, xor_1_out;

  not not_1 (not_1_out, A);
  not not_2 (not_2_out, A);
  xor xor_1 (xor_1_out, A, B);
  and and_1 (and_1_out, not_1_out, B);
  and and_2 (and_2_out, not_2_out, Cin, Cin);
  and and_3 (and_3_out, B, Cin);
  xor xor_2 (S, Cin, xor_1_out);
  or or_1 (Cout, and_1_out, and_2_out, and_3_out);

  // Notes on the sheet:
  //   Cin0
  //   A0
  //   B0
  //   S0
  //   Cin1
endmodule

module sub5 (
  input  in_1,
  input  in_2,
  input  in_3,
  input  in_4,
  input  in_5,
  input  in_6,
  input  in_7,
  input  in_8,
  input  in_9,
  output out_10
);

  wire subtrator_1_cout, subtrator_2_cout, subtrator_3_cout;

  SUBTRATOR subtrator_1 (.A(in_1), .Cin(in_5), .B(in_6), .Cout(subtrator_1_cout));  // open: S
  SUBTRATOR subtrator_2 (.A(in_2), .Cin(subtrator_1_cout), .B(in_7), .Cout(subtrator_2_cout));  // open: S
  SUBTRATOR subtrator_3 (.A(in_3), .Cin(subtrator_2_cout), .B(in_8), .Cout(subtrator_3_cout));  // open: S
  SUBTRATOR subtrator_4 (.A(in_4), .Cin(subtrator_3_cout), .B(in_9), .Cout(out_10));  // open: S
endmodule
