// Logisim project aula logisim .circ as structural Verilog: 1 circuit, main circuit main
module main (
  input  in_1,
  input  in_2,
  input  in_3,
  input  in_4,
  input  in_5,
  input  in_6,
  input  in_7,
  input  on_off,
  input  I0,
  input  in_10,
  input  in_11,
  input  I1,
  input  I2,
  input  I3,
  input  a0,
  input  a1,
  input  in_17,
  input  in_18,
  input  in_19,
  input  in_20,
  input  in_21,
  input  in_22,
  output out_23,
  output out_24,
  output O0,
  output out_26,
  output out_27,
  output out_28,
  output out_29,
  output out_30,
  output out_31
);

  wire and_1_out, and_2_out, and_5_out, and_6_out, and_7_out, and_8_out, not_1_out, not_2_out, not_3_out,
       not_4_out, not_5_out, not_6_out;

  not not_1 (not_1_out, in_6);
  and and_1 (and_1_out, in_1, not_1_out);
  and and_2 (and_2_out, in_4, in_6);
  not not_2 (not_2_out, in_19);
  or or_1 (out_23, and_1_out, and_2_out);
  and and_3 (out_27, in_17, not_2_out);
  and and_4 (out_29, in_17, in_19);
  not not_3 (not_3_out, in_10);
  not not_4 (not_4_out, in_11);
  not not_5 (not_5_out, in_20);
  and and_5 (and_5_out, in_2, not_3_out, not_4_out);
  and and_6 (and_6_out, in_3, not_3_out, in_11);
  and and_7 (and_7_out, in_5, in_10, not_4_out);
  and and_8 (and_8_out, in_7, in_10, in_11);
  not not_6 (not_6_out, in_21);
  and and_9 (out_26, in_18, not_5_out, not_6_out);
  and and_10 (out_28, in_18, not_5_out, in_21);
  and and_11 (out_30, in_18, in_20, not_6_out);
  and and_12 (out_31, in_18, in_20, in_21);
  or or_2 (out_24, and_5_out, and_6_out, and_7_out, and_8_out, and_8_out);
  // _74153 74153_1: pin names not known; wires that end beside it: on_off, a0, I0, I1, I2, I3, O0, 1'b0, 1'b1, a1

  // Notes on the sheet:
  //   DEMUX 1-2
  //   MUX 2-1
  //   DEMUX 1-4
  //   MUX 4-1
  //   ENTRADAS
  //   terra
  //   CI74153
  //   controladores
  //   fonte
endmodule
