// Logisim project shifters.circ as structural Verilog
module LSL (
  input  A3,
  input  A2,
  input  A1,
  input  A0,
  input  S1,
  input  S0,
  input  in_7,
  output out_8,
  output out_9,
  output out_10,
  output out_11
);

  MUX mux_1 (.I0(A3), .I1(A2), .I2(A1), .I3(A0), .S1(S1), .S0(S0), .out_7(out_8));
  MUX mux_2 (.I0(A2), .I1(A1), .I2(A0), .I3(in_7), .S1(S1), .S0(S0), .out_7(out_9));
  MUX mux_3 (.I0(A1), .I1(A0), .I2(in_7), .I3(in_7), .S1(S1), .S0(S0), .out_7(out_10));
  MUX mux_4 (.I0(A0), .I1(in_7), .I2(in_7), .I3(in_7), .S1(S1), .S0(S0), .out_7(out_11));

  // Notes on the sheet:
  //   DESLOCADOR À ESQUERDA
endmodule

module MUX (
  input  I0,
  input  I1,
  input  I2,
  input  I3,
  input  S1,
  input  S0,
  output out_7
);

  wire and_1_out, and_2_out, and_3_out, and_4_out, not_1_out, not_2_out, not_3_out;

  not not_1 (not_1_out, S1);
  and and_1 (and_1_out, I0, not_1_out, not_2_out);
  not not_2 (not_2_out, S0);
  and and_2 (and_2_out, I1, not_1_out, S0);
  and and_3 (and_3_out, I2, S1, not_3_out);
  not not_3 (not_3_out, S0);
  and and_4 (and_4_out, I3, S1, S0);
  or or_1 (out_7, and_1_out, and_2_out, and_3_out, and_4_out);
endmodule

module LSR (
  input  A3,
  input  A2,
  input  A1,
  input  A0,
  input  S1,
  input  S0,
  input  in_7,
  output out_8,
  output out_9,
  output out_10,
  output out_11
);

  MUX mux_1 (.I0(A3), .I1(in_7), .I2(in_7), .I3(in_7), .S1(S1), .S0(S0), .out_7(out_8));
  MUX mux_2 (.I0(A2), .I1(A3), .I2(in_7), .I3(in_7), .S1(S1), .S0(S0), .out_7(out_9));
  MUX mux_3 (.I0(A1), .I1(A2), .I2(A3), .I3(in_7), .S1(S1), .S0(S0), .out_7(out_10));
  MUX mux_4 (.I0(A0), .I1(A1), .I2(A2), .I3(A3), .S1(S1), .S0(S0), .out_7(out_11));
endmodule

module ASR (
  input  A3,
  input  A2,
  input  A1,
  input  A0,
  input  S1,
  input  S0,
  output out_7,
  output out_8,
  output out_9,
  output out_10
);

  MUX mux_1 (.I0(A3), .I1(A3), .I2(A3), .I3(A3), .S1(S1), .S0(S0), .out_7(out_7));
  MUX mux_2 (.I0(A2), .I1(A3), .I2(A3), .I3(A3), .S1(S1), .S0(S0), .out_7(out_8));
  MUX mux_3 (.I0(A1), .I1(A2), .I2(A3), .I3(A3), .S1(S1), .S0(S0), .out_7(out_9));
  MUX mux_4 (.I0(A0), .I1(A1), .I2(A2), .I3(A3), .S1(S1), .S0(S0), .out_7(out_10));
endmodule
